// Logisim project Lab1Q2.circ as structural Verilog: 1 circuit, main circuit main
module main (
  input  A,
  input  B,
  input  C,
  output out_4
);

  wire and_1_out, and_2_out, nand_1_out, not_1_out, or_1_out;

  not not_1 (not_1_out, A);
  nand nand_1 (nand_1_out, B, A);
  or or_1 (or_1_out, nand_1_out, C);
  and and_1 (and_1_out, not_1_out, C);
  and and_2 (and_2_out, not_1_out, or_1_out);
  xor xor_1 (out_4, and_1_out, and_2_out);

  // Notes on the sheet:
  //   F1
  //   İkinci devreyi çizicem
endmodule
